# Fritzing sketch FINAL FRITIZING FOR PROGRAMMING CLASS (saved by Fritzing 0.7.11b)
breadboards: 3

parts:
  Arduino1 = Arduino
  U1 = 74HC595 [package="DIP16 [THT]"]
  U2 = 74HC595 [package="DIP16 [THT]"]
  U3 = 74HC595 [package="DIP16 [THT]"]
  RHT1 = Humidity and Temperature Sensor RHT03
  R1 = Photocell (LDR) [package=THT]
  Part1 = Breakout Board for Electret Microphone
  LED1 = RGB LED (com. anode, rbg) [package="5 mm [THT]"]
  LED2 = RGB LED (com. anode, rbg) [package="5 mm [THT]"]
  LED3 = RGB LED (com. anode, rbg) [package="5 mm [THT]"]
  LED4 = RGB LED (com. anode, rbg) [package="5 mm [THT]"]
  LED5 = RGB LED (com. anode, rbg) [package="5 mm [THT]"]
  LED6 = RGB LED (com. anode, rbg) [package="5 mm [THT]"]
  LED7 = RGB LED (com. anode, rbg) [package="5 mm [THT]"]
  LED8 = RGB LED (com. anode, rbg) [package="5 mm [THT]"]
  R2 = Resistor [tolerance=±5% resistance=330 package=THT]
  R3 = Resistor [tolerance=±5% resistance=330 package=THT]
  R4 = Resistor [tolerance=±5% resistance=330 package=THT]
  R5 = Resistor [tolerance=±5% resistance=330 package=THT]
  R6 = Resistor [tolerance=±5% resistance=330 package=THT]
  R7 = Resistor [tolerance=±5% resistance=330 package=THT]
  R8 = Resistor [tolerance=±5% resistance=330 package=THT]
  R9 = Resistor [tolerance=±5% resistance=330 package=THT]
  R10 = Resistor [tolerance=±5% resistance=330 package=THT]
  R11 = Resistor [tolerance=±5% resistance=330 package=THT]
  R12 = Resistor [tolerance=±5% resistance=330 package=THT]
  R13 = Resistor [tolerance=±5% resistance=330 package=THT]
  R14 = Resistor [tolerance=±5% resistance=330 package=THT]
  R15 = Resistor [tolerance=±5% resistance=330 package=THT]
  R16 = Resistor [tolerance=±5% resistance=330 package=THT]
  R17 = Resistor [tolerance=±5% resistance=330 package=THT]
  R18 = Resistor [tolerance=±5% resistance=330 package=THT]
  R19 = Resistor [tolerance=±5% resistance=330 package=THT]
  R20 = Resistor [tolerance=±5% resistance=330 package=THT]
  R21 = Resistor [tolerance=±5% resistance=330 package=THT]
  R22 = Resistor [tolerance=±5% resistance=330 package=THT]
  R23 = Resistor [tolerance=±5% resistance=330 package=THT]
  R24 = Resistor [tolerance=±5% resistance=330 package=THT]
  R25 = Resistor [tolerance=±5% resistance=330 package=THT]
  C2 = Electrolytic Capacitor [capacitance=0.1µF package="100 mil [THT, electrolytic]"]
  R26 = Resistor [tolerance=±5% resistance=10k package=THT]
  R27 = Resistor [tolerance=±5% resistance=10k package=THT]

nets:
  N1: Arduino1.D12, U1.SH_CP, U2.SH_CP, U3.SH_CP
  N2: Arduino1.D11, U1.DS
  N3: Arduino1.D8, U1.ST_CP, U2.ST_CP, U3.ST_CP, C2.-
  N4: Arduino1.D3, LED1.common_anode, LED2.common_anode, LED3.common_anode, LED4.common_anode, LED5.common_anode, LED6.common_anode, LED7.common_anode, LED8.common_anode
  N5: Arduino1.D2, RHT1.Data-signal, R26.Pin_1
  VCC: Arduino1.+5V, RHT1.Vcc, Part1.VCC, R26.Pin_0, R27.Pin_0
  GND: Arduino1.GND, U1.GND, U1.OE, U2.GND, U2.OE, U3.GND, U3.OE, RHT1.GND_2, R1.pin_1, Part1.GND, C2.+
  N6: Arduino1.A0, R1.pin_0, R27.Pin_1
  N7: Arduino1.A1, Part1.AUD
  N8: U1.Q1, R7.Pin_1
  N9: U1.Q2, R10.Pin_1
  N10: U1.Q3, R13.Pin_1
  N11: U1.Q4, R16.Pin_1
  N12: U1.Q5, R19.Pin_1
  N13: U1.Q6, R22.Pin_1
  N14: U1.Q7, R25.Pin_1
  N15: U1.Q7', U2.DS
  VCC_2: U1.MR, U1.VCC, U2.MR, U2.VCC, U3.MR, U3.VCC, R4.Pin_1
  N16: U2.Q1, R5.Pin_1
  N17: U2.Q2, R8.Pin_1
  N18: U2.Q3, R11.Pin_1
  N19: U2.Q4, R14.Pin_1
  N20: U2.Q5, R17.Pin_1
  N21: U2.Q6, R20.Pin_1
  N22: U2.Q7, R23.Pin_1
  N23: U2.Q7', U3.DS
  N24: U2.Q0, R2.Pin_1
  N25: U3.Q1, R6.Pin_1
  N26: U3.Q2, R9.Pin_1
  N27: U3.Q3, R12.Pin_1
  N28: U3.Q4, R15.Pin_1
  N29: U3.Q5, R18.Pin_1
  N30: U3.Q6, R21.Pin_1
  N31: U3.Q7, R24.Pin_1
  N32: U3.Q0, R3.Pin_1
  N33: LED1.red_cathode, R4.Pin_0
  N34: LED1.blue_cathode, R3.Pin_0
  N35: LED1.green_cathode, R2.Pin_0
  N36: LED2.red_cathode, R7.Pin_0
  N37: LED2.blue_cathode, R6.Pin_0
  N38: LED2.green_cathode, R5.Pin_0
  N39: LED3.red_cathode, R10.Pin_0
  N40: LED3.blue_cathode, R9.Pin_0
  N41: LED3.green_cathode, R8.Pin_0
  N42: LED4.red_cathode, R13.Pin_0
  N43: LED4.blue_cathode, R12.Pin_0
  N44: LED4.green_cathode, R11.Pin_0
  N45: LED5.red_cathode, R16.Pin_0
  N46: LED5.blue_cathode, R15.Pin_0
  N47: LED5.green_cathode, R14.Pin_0
  N48: LED6.red_cathode, R19.Pin_0
  N49: LED6.blue_cathode, R18.Pin_0
  N50: LED6.green_cathode, R17.Pin_0
  N51: LED7.red_cathode, R22.Pin_0
  N52: LED7.blue_cathode, R21.Pin_0
  N53: LED7.green_cathode, R20.Pin_0
  N54: LED8.red_cathode, R25.Pin_0
  N55: LED8.blue_cathode, R24.Pin_0
  N56: LED8.green_cathode, R23.Pin_0
