# Fritzing sketch Prototype FINAL (saved by Fritzing 0.7.12b)
breadboards: 1

parts:
  RHT1 = Humidity and Temperature Sensor RHT03
  R1 = Photocell (LDR) [package=THT]
  C1 = Electrolytic Capacitor [capacitance=10µF package="100 mil [THT, electrolytic]"]
  LED1 = RGB LED (com. anode, rbg) [package="5 mm [THT]"]
  Arduino1 = Arduino
  R2 = Resistor [tolerance=±5% resistance=10k package=THT]
  R3 = Resistor [tolerance=±5% resistance=10k package=THT]
  Part1 = Breakout Board for Electret Microphone
  R4 = Resistor [tolerance=±5% resistance=220 package=THT]
  R5 = Resistor [tolerance=±5% resistance=330 package=THT]
  R6 = Resistor [tolerance=±5% resistance=330 package=THT]
  R7 = Resistor [tolerance=±5% resistance=330 package=THT]

nets:
  VCC: RHT1.Vcc, R1.pin_1, Arduino1.+5V, R2.Pin_0
  N1: RHT1.Data-signal, Arduino1.D2, R2.Pin_1
  N2: RHT1.GND_2, C1.+, LED1.common_anode, Arduino1.GND, R3.Pin_0, Part1.AUD, R4.Pin_1
  N3: R1.pin_0, Arduino1.A0, R3.Pin_1
  N4: C1.-, Arduino1.A1, Part1.VCC
  N5: LED1.red_cathode, R5.Pin_1
  N6: LED1.blue_cathode, R6.Pin_1
  N7: LED1.green_cathode, R7.Pin_1
  N8: Arduino1.D6, R7.Pin_0
  N9: Arduino1.D5, R6.Pin_0
  N10: Arduino1.D3, R5.Pin_0
  N11: Part1.GND, R4.Pin_0
